// Logisim project task1.circ as structural Verilog: 2 circuits, main circuit main
module main (
  input  in_1,
  input  in_2,
  input  in_3,
  input  in_4,
  input  in_5,
  input  in_6,
  input  in_7,
  input  in_8,
  input  in_9,
  input  in_10,
  input  in_11,
  input  in_12,
  input  in_13,
  input  in_14,
  input  in_15,
  input  in_16,
  input  x1,
  output out_18,
  output out_19,
  output out_20,
  output out_21,
  output out_22,
  output out_23,
  output out_24,
  output out_25,
  output out_26
);

  wire and_1_out, and_2_out, and_3_out, and_4_out, and_5_out, and_6_out, and_7_out, and_8_out, and_9_out,
       and_10_out, and_11_out, and_12_out, and_13_out, and_14_out, and_15_out, and_16_out, and_17_out,
       and_18_out, and_19_out, and_20_out, and_21_out, and_22_out, and_23_out, and_24_out, car1_out,
       car2_out, car3_out, car4_out, car5_out, car6_out, car7_out, or_1_out, or_2_out, or_3_out, or_4_out,
       or_5_out, or_6_out, or_7_out, or_8_out, xor_1_out, xor_2_out, xor_3_out, xor_4_out, xor_5_out,
       xor_6_out, xor_7_out, xor_8_out;

  xor xor_1 (xor_1_out, in_9, car7_out);
  and and_1 (and_1_out, in_9, in_1);
  and and_2 (and_2_out, in_9, car7_out);
  and and_3 (and_3_out, in_1, car7_out);
  xor ones8 (out_19, in_1, xor_1_out);
  or or_1 (or_1_out, and_1_out, and_2_out);
  or car8 (out_18, or_1_out, and_3_out);
  xor xor_2 (xor_2_out, in_10, car6_out);
  and and_4 (and_4_out, in_10, in_2);
  and and_5 (and_5_out, in_10, car6_out);
  and and_6 (and_6_out, in_2, car6_out);
  xor ones7 (out_20, in_2, xor_2_out);
  or or_2 (or_2_out, and_4_out, and_5_out);
  or car7 (car7_out, or_2_out, and_6_out);
  xor xor_3 (xor_3_out, in_11, car5_out);
  and and_7 (and_7_out, in_11, in_3);
  and and_8 (and_8_out, in_11, car5_out);
  and and_9 (and_9_out, in_3, car5_out);
  xor ones6 (out_21, in_3, xor_3_out);
  or or_3 (or_3_out, and_7_out, and_8_out);
  or car6 (car6_out, or_3_out, and_9_out);
  halfadder halfadder_1 ();  // open: x1, x2, x3, ones, car
  xor xor_4 (xor_4_out, in_12, car4_out);
  and and_10 (and_10_out, in_12, in_4);
  and and_11 (and_11_out, in_12, car4_out);
  and and_12 (and_12_out, in_4, car4_out);
  xor ones5 (out_22, in_4, xor_4_out);
  or or_4 (or_4_out, and_10_out, and_11_out);
  or car5 (car5_out, or_4_out, and_12_out);
  xor xor_5 (xor_5_out, in_13, car3_out);
  and and_13 (and_13_out, in_13, in_5);
  and and_14 (and_14_out, in_13, car3_out);
  and and_15 (and_15_out, in_5, car3_out);
  xor ones4 (out_23, in_5, xor_5_out);
  or or_5 (or_5_out, and_13_out, and_14_out);
  or car4 (car4_out, or_5_out, and_15_out);
  xor xor_6 (xor_6_out, in_14, car2_out);
  and and_16 (and_16_out, in_14, in_6);
  and and_17 (and_17_out, in_14, car2_out);
  and and_18 (and_18_out, in_6, car2_out);
  xor ones3 (out_24, in_6, xor_6_out);
  or or_6 (or_6_out, and_16_out, and_17_out);
  or car3 (car3_out, or_6_out, and_18_out);
  xor xor_7 (xor_7_out, in_15, car1_out);
  and and_19 (and_19_out, in_15, in_7);
  and and_20 (and_20_out, in_15, car1_out);
  and and_21 (and_21_out, in_7, car1_out);
  xor ones2 (out_25, in_7, xor_7_out);
  or or_7 (or_7_out, and_19_out, and_20_out);
  or car2 (car2_out, or_7_out, and_21_out);
  xor xor_8 (xor_8_out, in_16, x1);
  and and_22 (and_22_out, in_16, in_8);
  and and_23 (and_23_out, in_16, x1);
  and and_24 (and_24_out, in_8, x1);
  xor ones1 (out_26, in_8, xor_8_out);
  or or_8 (or_8_out, and_22_out, and_23_out);
  or car1 (car1_out, or_8_out, and_24_out);

  // Notes on the sheet:
  //   x2
  //   x3
  //   x1
  //   x2
  //   x1
  //   x3
  //   x2
  //   x3
  //   x1
  //   x3
  //   x1
  //   x2
  //   x3
  //   x2
  //   x1
  //   x3
  //   x2
  //   x1
  //   x3
  //   x2
  //   x1
  //   x3
  //   x2
endmodule

module halfadder (
  input  x1,
  input  x2,
  input  x3,
  output ones,
  output car
);

  wire and_1_out, and_2_out, and_3_out, or_1_out, xor_1_out;

  xor xor_1 (xor_1_out, x2, x3);
  and and_1 (and_1_out, x2, x1);
  and and_2 (and_2_out, x2, x3);
  and and_3 (and_3_out, x1, x3);
  xor ones4 (ones, x1, xor_1_out);
  or or_1 (or_1_out, and_1_out, and_2_out);
  or car4 (car, or_1_out, and_3_out);
endmodule
