// Logisim project task1b.circ as structural Verilog: 2 circuits, main circuit main
module main (
  input  in_1,
  input  in_2,
  input  in_3,
  input  in_4,
  input  in_5,
  input  in_6,
  input  in_7,
  input  in_8,
  input  in_9,
  input  in_10,
  input  in_11,
  input  in_12,
  input  in_13,
  input  in_14,
  input  in_15,
  input  in_16,
  input  in_17,
  output out_18,
  output out_19,
  output out_20,
  output out_21,
  output out_22,
  output out_23,
  output out_24,
  output out_25,
  output out_26
);

  wire halfadder_2_car, halfadder_3_car, halfadder_4_car, halfadder_5_car, halfadder_6_car, halfadder_7_car,
       halfadder_8_car;

  halfadder halfadder_1 (.x1(in_1), .x2(in_9), .x3(halfadder_2_car), .ones(out_19), .car(out_18));
  halfadder halfadder_2 (.x1(in_2), .x2(in_10), .x3(halfadder_3_car), .ones(out_20), .car(halfadder_2_car));
  halfadder halfadder_3 (.x1(in_3), .x2(in_11), .x3(halfadder_4_car), .ones(out_21), .car(halfadder_3_car));
  halfadder halfadder_4 (.x1(in_4), .x2(in_12), .x3(halfadder_5_car), .ones(out_22), .car(halfadder_4_car));
  halfadder halfadder_5 (.x1(in_5), .x2(in_13), .x3(halfadder_6_car), .ones(out_23), .car(halfadder_5_car));
  halfadder halfadder_6 (.x1(in_6), .x2(in_14), .x3(halfadder_7_car), .ones(out_24), .car(halfadder_6_car));
  halfadder halfadder_7 (.x1(in_7), .x2(in_15), .x3(halfadder_8_car), .ones(out_25), .car(halfadder_7_car));
  halfadder halfadder_8 (.x1(in_8), .x2(in_16), .x3(in_17), .ones(out_26), .car(halfadder_8_car));
endmodule

module halfadder (
  input  x1,
  input  x2,
  input  x3,
  output ones,
  output car
);

  wire and_1_out, and_2_out, and_3_out, or_1_out, xor_1_out;

  xor xor_1 (xor_1_out, x2, x3);
  and and_1 (and_1_out, x2, x1);
  and and_2 (and_2_out, x2, x3);
  and and_3 (and_3_out, x1, x3);
  xor ones4 (ones, x1, xor_1_out);
  or or_1 (or_1_out, and_1_out, and_2_out);
  or car4 (car, or_1_out, and_3_out);
endmodule
