// Logisim project task3.circ as structural Verilog: 1 circuit, main circuit main
module main (
  input  in_1,
  output out_2,
  output out_3,
  output out_4
);

  wire a1_out, a2_out, clock_1_out, nand_1_out, nand_2_out;

  Clock clock_1 (.out(clock_1_out));
  T_Flip_Flop t_ff_1 (.T(nand_2_out), .clk(clock_1_out), .Q(out_2));  // open: Qn, reset, preset
  T_Flip_Flop t_ff_2 (.T(a2_out), .clk(clock_1_out), .Q(out_3));  // open: Qn, reset, preset
  T_Flip_Flop t_ff_3 (.T(in_1), .clk(clock_1_out), .Q(out_4));  // open: Qn, reset, preset
  nand a1 (a1_out, out_3, out_3);
  nand a2 (a2_out, out_4, out_4);
  nand nand_1 (nand_1_out, a1_out, a2_out);
  nand nand_2 (nand_2_out, nand_1_out, nand_1_out);
endmodule
