// Logisim project task1.circ as structural Verilog: 1 circuit, main circuit main
module main (
  input  in_1,
  input  A,
  input  in_3,
  input  B,
  input  in_5,
  input  Zin
);
endmodule
